# Fritzing sketch HomeAwayHome-CircuitDiagram (saved by Fritzing 1.0.5)
breadboards: 1

parts:
  Part1 = Arduino Nano 33 IOT
  HC-SR04_Sensor_1 = HC-SR04 Ultrasonic Distance Sensor
  R1 = Resistor [tolerance=±5% resistance=10k package="1206 [SMD]"]
  J1 = Piezo Speaker
  LED1 = smd LED [color="Red (633nm)" current=0A package="0805 [SMD]"]

nets:
  N1: Part1.TX, Part1.D2, HC-SR04_Sensor_1.TRIG
  N2: Part1.RESET, Part1.A7
  GND: Part1.GND, Part1.D13~, HC-SR04_Sensor_1.GND, J1.pin1, LED1.cathode
  N3: Part1.D3~, R1.Pin_0
  N4: Part1.D9~, LED1.anode
  N5: Part1.D11/MOSI, Part1.+5V, J1.pin2
  3V3: Part1.3V3, HC-SR04_Sensor_1.VCC
  N6: HC-SR04_Sensor_1.ECHO, R1.Pin_1

custom parts:
  Arduino Nano 33 IOT: The Arduino Nano 33 IoT is the easiest and cheapest point of entry to enhance existing devices (and creating new ones) to be part of the IoT and designing pico-network applications. Whether you are looking at building a sensor network connected to your office or home router, or if you want to create a BLE device sending data to a cellphone, the Nano 33 IoT is your one-stop-solution for many of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
